// Digital circuit frontpanel.dig as structural Verilog
module frontpanel (
  input  clock,
  input  run,
  output [15:0] R0,
  output [15:0] R1,
  output [15:0] R2,
  output [15:0] R3,
  output [7:0] PC,
  output halt,
  output error
);

  wire control_1_p5, control_1_p6, control_1_p11, control_1_p12, decoder_1_p3, execute_1_p4, hex,
       hexdisplay_1_p2, hexdisplay_1_p5, hexdisplay_1_p8, hexdisplay_1_p10, hexdisplay_1_p13,
       hexdisplay_2_p2, hexdisplay_2_p5, hexdisplay_2_p8, hexdisplay_2_p10, hexdisplay_2_p13,
       instrdisplay_1_p2, instrdisplay_1_p4, instrdisplay_1_p7, instrdisplay_1_p9, instrdisplay_1_p12,
       instrdisplay_1_p14, jump, L, memaccess_1_p9, op, pmshim_1_p4, pmshim_1_p5, pmshim_1_p6, rd_valid,
       regdisplay_1_p1, regdisplay_1_p2, regdisplay_2_p1, regdisplay_2_p2, rs_valid, run_out, S, step_out,
       sys, T;
  wire [1:0] rd, rs;
  wire [3:0] hexdisplay_1_p1, hexdisplay_1_p4, hexdisplay_1_p6, hexdisplay_1_p9, hexdisplay_1_p12,
       hexdisplay_2_p1, hexdisplay_2_p4, hexdisplay_2_p6, hexdisplay_2_p9, hexdisplay_2_p12;
  wire [7:0] pmshim_1_p2;
  wire [15:0] decoder_1_p1, decoder_1_p2, fetch_1_instr_o, instrdisplay_1_p1, instrdisplay_1_p3,
       instrdisplay_1_p6, instrdisplay_1_p8, instrdisplay_1_p10, instrdisplay_1_p13, memaccess_1_p5,
       memaccess_1_p6, memaccess_1_p7, memaccess_1_p8, pmshim_1_p3, Program_d, R, regdisplay_1_d1,
       regdisplay_1_d2, regdisplay_2_d1, regdisplay_2_d2;

  // pmshim pmshim_1: pin names not known; wires that end beside it: PC, pmshim_1_p2, pmshim_1_p3, pmshim_1_p4, pmshim_1_p5, pmshim_1_p6
  EEPROMDualPort #(.AddrBits(8), .isProgramMemory("true"), .Bits(16)) Program (
    .A(pmshim_1_p2), .Din(pmshim_1_p3), .str(pmshim_1_p4), .C(pmshim_1_p5), .ld(pmshim_1_p6), .D(Program_d));
  Button step (.out(step_out));
  Button u_run (.out(run_out));
  clockctrl clockctrl_1 (.clock(clock), .step(step_out), .fast(run_out), .faster(run), .stall(S));  // open: slow
  fetch fetch_1 (
    .instr_i(Program_d), .clock(clock), .en(control_1_p12), .jump(jump), .value(R), .pc(PC),
    .instr_o(fetch_1_instr_o));
  SixteenSeg sixteenseg_1 (.led(regdisplay_1_d1), .dp(regdisplay_1_p1));
  SixteenSeg sixteenseg_2 (.led(regdisplay_1_d2), .dp(regdisplay_1_p2));
  regdisplay regdisplay_1 (
    .D1(regdisplay_1_d1), .P1(regdisplay_1_p1), .D2(regdisplay_1_d2), .P2(regdisplay_1_p2), .E(1'b1),
    .J(jump), .R(rd));
  // decoder decoder_1: pin names not known; wires that end beside it: decoder_1_p1, decoder_1_p2, decoder_1_p3, fetch_1_instr_o, rs, rd, L, R, sys, op, rs_valid, rd_valid
  Seven_Seg_Hex seven_seg_hex_1 (.d(hexdisplay_1_p1), .dp(hexdisplay_1_p2));
  Seven_Seg_Hex seven_seg_hex_2 (.d(hexdisplay_1_p4), .dp(hexdisplay_1_p5));
  // hexdisplay hexdisplay_1: pin names not known; wires that end beside it: hexdisplay_1_p1, hexdisplay_1_p2, rd_valid, hexdisplay_1_p4, hexdisplay_1_p5, hexdisplay_1_p6, L, hexdisplay_1_p8, hexdisplay_1_p9, hexdisplay_1_p10, hex, hexdisplay_1_p12, hexdisplay_1_p13
  Seven_Seg_Hex seven_seg_hex_3 (.d(hexdisplay_1_p6), .dp(hexdisplay_1_p8));
  Seven_Seg_Hex seven_seg_hex_4 (.d(hexdisplay_1_p9), .dp(hexdisplay_1_p10));
  Seven_Seg_Hex seven_seg_hex_5 (.d(hexdisplay_1_p12), .dp(hexdisplay_1_p13));
  // control control_1: pin names not known; wires that end beside it: sys, op, S, clock, control_1_p5, control_1_p6, T, halt, error, decoder_1_p3, control_1_p11, control_1_p12, jump
  SixteenSeg sixteenseg_3 (.led(instrdisplay_1_p1), .dp(instrdisplay_1_p2));
  SixteenSeg sixteenseg_4 (.led(instrdisplay_1_p3), .dp(instrdisplay_1_p4));
  // instrdisplay instrdisplay_1: pin names not known; wires that end beside it: instrdisplay_1_p1, instrdisplay_1_p2, instrdisplay_1_p3, instrdisplay_1_p4, sys, instrdisplay_1_p6, instrdisplay_1_p7, instrdisplay_1_p8, instrdisplay_1_p9, instrdisplay_1_p10, op, instrdisplay_1_p12, instrdisplay_1_p13, instrdisplay_1_p14
  SixteenSeg sixteenseg_5 (.led(instrdisplay_1_p6), .dp(instrdisplay_1_p7));
  SixteenSeg sixteenseg_6 (.led(instrdisplay_1_p8), .dp(instrdisplay_1_p9));
  SixteenSeg sixteenseg_7 (.led(instrdisplay_1_p10), .dp(instrdisplay_1_p12));
  SixteenSeg sixteenseg_8 (.led(instrdisplay_1_p13), .dp(instrdisplay_1_p14));
  // execute execute_1: pin names not known; wires that end beside it: L, R, control_1_p6, execute_1_p4, control_1_p5
  Seven_Seg_Hex seven_seg_hex_6 (.d(hexdisplay_2_p1), .dp(hexdisplay_2_p2));
  Seven_Seg_Hex seven_seg_hex_7 (.d(hexdisplay_2_p4), .dp(hexdisplay_2_p5));
  // hexdisplay hexdisplay_2: pin names not known; wires that end beside it: hexdisplay_2_p1, hexdisplay_2_p2, 1'b1, hexdisplay_2_p4, hexdisplay_2_p5, hexdisplay_2_p6, R, hexdisplay_2_p8, hexdisplay_2_p9, hexdisplay_2_p10, hex, hexdisplay_2_p12, hexdisplay_2_p13
  // memaccess memaccess_1: pin names not known; wires that end beside it: execute_1_p4, decoder_1_p1, decoder_1_p3, control_1_p11, memaccess_1_p5, memaccess_1_p6, memaccess_1_p7, memaccess_1_p8, memaccess_1_p9
  Seven_Seg_Hex seven_seg_hex_8 (.d(hexdisplay_2_p6), .dp(hexdisplay_2_p8));
  Seven_Seg_Hex seven_seg_hex_9 (.d(hexdisplay_2_p9), .dp(hexdisplay_2_p10));
  DipSwitch u_hex (.out(hex));
  Seven_Seg_Hex seven_seg_hex_10 (.d(hexdisplay_2_p12), .dp(hexdisplay_2_p13));
  SixteenSeg sixteenseg_9 (.led(regdisplay_2_d1), .dp(regdisplay_2_p1));
  SixteenSeg sixteenseg_10 (.led(regdisplay_2_d2), .dp(regdisplay_2_p2));
  regdisplay regdisplay_2 (
    .D1(regdisplay_2_d1), .P1(regdisplay_2_p1), .D2(regdisplay_2_d2), .P2(regdisplay_2_p2), .E(rs_valid),
    .J(1'b0), .R(rs));
  regfile regfile_1 (
    .rs(rs), .rd(rd), .result(memaccess_1_p6), .clock(clock), .RL(decoder_1_p1), .RR(decoder_1_p2), .R0(R0),
    .R1(R1), .R2(R2), .R3(R3));
  RAMDualPort #(.AddrBits(16), .Bits(16)) Data (
    .A(memaccess_1_p7), .Din(memaccess_1_p8), .str(memaccess_1_p9), .C(clock), .ld(1'b1), .D(memaccess_1_p5));
  LED u_T (.in(T));

  // Other names for the same wires on the sheet: C = clock; erun = run

  // Notes on the sheet:
  //   clock: Hz: 10
  //   contents of Program (hex, n*v repeats v):
  //   303,30b,b13,8092,b11a,1d,810a,b09a,81d,1c,1003,61
  //   rj45 Creates
endmodule
